# Fritzing sketch nano-led-poi (saved by Fritzing 0.9.2b)
breadboards: 1

parts:
  Part1 = Arduino Nano (Rev3.0)
  GY1 = MPU-6050 Board GY-521 [form="♀ (female)" package=THT]
  LED1 = RGB LED - (4 legs) [package="5 mm [THT]"]
  R1 = Resistor [tolerance=±5% resistance=220 package="2010 [SMD]"]
  R2 = Resistor [tolerance=±5% resistance=220 package="0402 [SMD]"]
  R3 = Resistor [tolerance=±5% resistance=220 package="0402 [SMD]"]

nets:
  N1: Part1.GND, GY1.pin2
  N2: Part1.D2, GY1.pin8
  N3: Part1.D8, R2.Pin_0
  N4: Part1.D9, R3.Pin_0
  N5: Part1.D10, R1.Pin_0
  N6: Part1.5V, GY1.pin1
  N7: Part1.A5, GY1.pin3
  N8: Part1.A4, GY1.pin4
  N9: LED1.red_cathode, R2.Pin_1
  N10: LED1.green_cathode, R3.Pin_1
  N11: LED1.blue_cathode, R1.Pin_1

custom parts:
  MPU-6050 Board GY-521: Acelerometro y Giroscopio MPU-6050 Board GY-521
