# Fritzing sketch ledtomusic-TH (saved by Fritzing 0.9.2b)
circuit board: 8.46667cm x 5.64444cm
breadboards: 1

parts:
  rgb_led_strip = RGB LED - (4 legs) [package="5 mm [THT]"]
  Part1 = Arduino Uno (Rev3)
  Q1 = Basic FET N-Channel [package="D2Pak [SMD]"]
  Q2 = Basic FET N-Channel [package="D2Pak [SMD]"]
  Q3 = Basic FET N-Channel [package="D2Pak [SMD]"]
  R1 = Resistor [tolerance=±5% resistance=10k package=THT]
  R2 = Resistor [tolerance=±5% resistance=10k package=THT]
  R3 = Resistor [tolerance=±5% resistance=10k package=THT]
  IC1 = MSGEQ7 [package=soic8]
  C1 = Ceramic Capacitor [capacitance=100nF package="100 mil [THT, multilayer]"]
  C2 = Ceramic Capacitor [capacitance=33pF package="100 mil [THT, multilayer]"]
  C3 = Ceramic Capacitor [capacitance=100nF package="100 mil [THT, multilayer]"]
  C4 = Ceramic Capacitor [capacitance=10nF package="100 mil [THT, multilayer]"]
  R4 = Resistor [tolerance=±5% resistance=220 package=THT]
  TRS1 = Audio Jack (TRS) 3.5mm [package="PG203J [THT]"]

nets:
  N1: rgb_led_strip.red_cathode, Q3.drain, R3.Pin_0
  N2: rgb_led_strip.common_anode, Q2.drain, R2.Pin_0
  N3: rgb_led_strip.green_cathode, Q1.drain, R1.Pin_0
  N4: rgb_led_strip.blue_cathode, Part1.VIN
  N5: Part1.A0, IC1.DCOUT
  N6: Part1.D9_PWM, Q3.Gate
  N7: Part1.D10_PWM/SS, Q2.Gate
  N8: Part1.D11_PWM/MOSI, Q1.Gate
  GND: Part1.GND, Q1.source, Q2.source, Q3.source, R1.Pin_1, R2.Pin_1, R3.Pin_1, IC1.GND, C1.1, C2.0, C3.1, TRS1.Sleeve
  N9: Part1.D2, IC1.STROBE
  N10: Part1.D4, IC1.RESET
  5V: Part1.5V, IC1.VDD, C1.0, R4.Pin_0
  N11: IC1.AUDIO_IN, C4.0
  N12: IC1.CG, C3.0
  N13: IC1.CKIN, C2.1, R4.Pin_1
  N14: C4.1, TRS1.Ring

notes:
  220k
  resistor
  C1 C2
  C3
  C4
  C1: 33pF
  C2: 100nF
  C3: 10nF
  C4: 100nF
  10k resistors
  make sure to plug the correct colored wire into the correct port on your led strip
  3.5 mm audio in goes here
  \/ \/ \/

// code stored in the sketch: ledtomusicc.ino
/* David Wang
 * Code that takes audio input from a 3.5mm cable
 * and flashes an LED strip based on the frequency
 * of the music.
 *
 * HUGE thanks to the arduino community
 * If you see your code here, I owe you my gratitude
 *
 */
// MODIFY SETTINGS TO WHAT EVER WORKS BEST FOR YOU!
 
int analogPin = 0; // MSGEQ7 OUT
int strobePin = 2; // MSGEQ7 STROBE
int resetPin = 4; // MSGEQ7 RESET
int spectrumValue[7];
 
// MSGEQ7 OUT pin produces values around 50-80
// when there is no input, so use this value to
// filter out a lot of the chaff.
int filterValue = 80;
 
// LED pins connected to the PWM pins on the Arduino
 
int ledPinR = 10;
int ledPinG = 9;
int ledPinB = 11;
 
void setup()
{
  //Serial.begin(9600);
  // Read from MSGEQ7 OUT
  pinMode(analogPin, INPUT);
  // Write to MSGEQ7 STROBE and RESET
  pinMode(strobePin, OUTPUT);
  pinMode(resetPin, OUTPUT);
 
  // Set analogPin's reference voltage
  analogReference(DEFAULT); // 5V
 
  // Set startup values for pins
  digitalWrite(resetPin, LOW);
  digitalWrite(strobePin, HIGH);
}
 
void loop()
{
  // Set reset pin low to enable strobe
  digitalWrite(resetPin, HIGH);
  digitalWrite(resetPin, LOW);
 
  // Get all 7 spectrum values from the MSGEQ7
  for (int i = 0; i < 7; i++)
  {
    digitalWrite(strobePin, LOW);
    delayMicroseconds(30); // Allow output to settle
 
    spectrumValue[i] = analogRead(analogPin);
 
    // Constrain any value above 1023 or below filterValue
    spectrumValue[i] = constrain(spectrumValue[i], filterValue, 1023);
 
 
    // Remap the value to a number between 0 and 255
    spectrumValue[i] = map(spectrumValue[i], filterValue, 1023, 0, 255);
 
    // Remove serial stuff after debugging
    //Serial.print(spectrumValue[i]);
    //Serial.print(" ");
    digitalWrite(strobePin, HIGH);
   }
 
   //Serial.println();
 
   // Write the PWM values to the LEDs
   // I find that with three LEDs, these three spectrum values work the best
   analogWrite(ledPinR, spectrumValue[1]);
   analogWrite(ledPinG, spectrumValue[4]);
   analogWrite(ledPinB, spectrumValue[6]);
}
