# Fritzing sketch uno-music-leds-perf (saved by Fritzing 0.9.2b)
circuit board: 8.53413cm x 4.61426cm
circuit board: 2.96045cm x 3.25782cm
circuit board: 2.03071cm x 1.81934cm
perfboards: 2

parts:
  rgb_led_strip = RGB LED - (4 legs) [part_number="RGB LED strip 5050" package="5 mm [THT]"]
  Arduino = Arduino Uno (Rev3)  # not connected
  Q1 = Basic FET N-Channel [part_number="RFP50N06 50N06 POWER MOSFET N-CHANNEL 60V 50A" package="D2Pak [SMD]"]
  Q2 = Basic FET N-Channel [part_number="RFP50N06 50N06 POWER MOSFET N-CHANNEL 60V 50A" package="D2Pak [SMD]"]
  Q3 = Basic FET N-Channel [part_number="RFP50N06 50N06 POWER MOSFET N-CHANNEL 60V 50A" package="D2Pak [SMD]"]
  R2 = Resistor [tolerance=±5% resistance=10k package=THT]
  R3 = Resistor [tolerance=±5% resistance=10k package=THT]
  TRS1 = Audio Jack (TRS) 3.5mm [package="PG203J [THT]"]
  R1 = Resistor [tolerance=±5% resistance=10k package=THT]
  MSGEQ8 = IC, DIP package, 8 pins [chip_label=MSGEQ7]
  C5 = Ceramic Capacitor [capacitance=100nF voltage=6.3V package="100 mil [THT, multilayer]"]
  C6 = Ceramic Capacitor [capacitance=10nF package="100 mil [THT, multilayer]"]
  C7 = Ceramic Capacitor [capacitance=100nF package="100 mil [THT, multilayer]"]
  R5 = Resistor [tolerance=±5% resistance=220k package=THT]
  C8 = Ceramic Capacitor [capacitance=33pF package="100 mil [THT, multilayer]"]

nets:
  N1: rgb_led_strip.red_cathode, Q1.drain, R1.Pin_0
  N2: rgb_led_strip.common_anode, Q2.drain, R2.Pin_0
  N3: rgb_led_strip.green_cathode, Q3.drain, R3.Pin_0
  N4: Q1.source, Q2.source, Q3.source, R2.Pin_1, R3.Pin_1, R1.Pin_1
  N5: TRS1.Ring, C6.0
  N6: MSGEQ8.pin1, C5.0, R5.Pin_0
  N7: MSGEQ8.pin2, C5.1
  N8: MSGEQ8.pin5, C6.1
  N9: MSGEQ8.pin6, C7.1
  N10: MSGEQ8.pin8, R5.Pin_1, C8.1
  N11: C7.0, C8.0

notes:
  R4 220k
  resistor
  C1 C2
  C3
  C4
  C1: 33pF
  C2: 100nF
  C3: 10nF
  C4: 100nF
  R1-R3 10k resistors
  LED strip
  audio in
  DC 12V, 5A

// code stored in the sketch: ledtomusicc.ino
/* David Wang
 * Code that takes audio input from a 3.5mm cable
 * and flashes an LED strip based on the frequency
 * of the music.
 *
 * HUGE thanks to the arduino community
 * If you see your code here, I owe you my gratitude
 *
 */
// MODIFY SETTINGS TO WHAT EVER WORKS BEST FOR YOU!
 
int analogPin = 0; // MSGEQ7 OUT
int strobePin = 2; // MSGEQ7 STROBE
int resetPin = 4; // MSGEQ7 RESET
int spectrumValue[7];
 
// MSGEQ7 OUT pin produces values around 50-80
// when there is no input, so use this value to
// filter out a lot of the chaff.
int filterValue = 80;
 
// LED pins connected to the PWM pins on the Arduino 
int ledPinR = 10;
int ledPinG = 9;
int ledPinB = 11;
 
void setup()
{
  // Read from MSGEQ7 OUT
  pinMode(analogPin, INPUT);

  // Write to MSGEQ7 STROBE and RESET
  pinMode(strobePin, OUTPUT);
  pinMode(resetPin, OUTPUT);
 
  // Set analogPin's reference voltage
  analogReference(DEFAULT); // 5V
 
  // Set startup values for pins
  digitalWrite(resetPin, LOW);
  digitalWrite(strobePin, HIGH);
}
 
void loop()
{
  // Set reset pin low to enable strobe
  digitalWrite(resetPin, HIGH);
  digitalWrite(resetPin, LOW);
 
  // Get all 7 spectrum values from the MSGEQ7
  for (int i = 0; i < 7; i++)
  {
    digitalWrite(strobePin, LOW);
    delayMicroseconds(30); // Allow output to settle
 
    spectrumValue[i] = analogRead(analogPin);
 
    // Constrain any value above 1023 or below filterValue
    spectrumValue[i] = constrain(spectrumValue[i], filterValue, 1023);
 
    // Remap the value to a number between 0 and 255
    spectrumValue[i] = map(spectrumValue[i], filterValue, 1023, 0, 255);
 
    digitalWrite(strobePin, HIGH);
   }
 
   // Write the PWM values to the LEDs

	 //TODO: combine spectrum values, eg: eq 1+2 for blue, 3+4+5 for red, 6+7 for green
   analogWrite(ledPinR, spectrumValue[1]);
   analogWrite(ledPinG, spectrumValue[4]);
   analogWrite(ledPinB, spectrumValue[6]);
}
